// Logisim project Flappy.circ as structural Verilog: 10 circuits, main circuit main
module main (
);

  wire and_1_out, button_2_out, button_out, clock_1_out, collisione_muri_1_out_3;
  wire [7:0] punteggio_1_out_3;
  wire [14:0] fsm_1_out_4, movimento_muri_1_out_4, movimento_muri_1_out_5, movimento_muri_1_out_6,
       movimento_muri_1_out_7, movimento_muri_1_out_8, movimento_muri_1_out_9, movimento_muri_1_out_10,
       movimento_muri_1_out_11, movimento_muri_1_out_12, movimento_muri_1_out_13, movimento_muri_1_out_14,
       movimento_muri_1_out_15, movimento_muri_1_out_16, movimento_muri_1_out_17, movimento_muri_1_out_18,
       movimento_muri_1_out_19, movimento_muri_1_out_20, movimento_muri_1_out_21, movimento_muri_1_out_22,
       movimento_muri_1_out_23, movimento_muri_1_out_24, movimento_muri_1_out_25, movimento_muri_1_out_26,
       movimento_muri_1_out_27, movimento_muri_1_out_28;

  Button button (.out(button_out));
  Button button_2 (.out(button_2_out));
  Collisione_muri collisione_muri_1 (
    .Posizione_personaggio(fsm_1_out_4), .Posizione_muro(movimento_muri_1_out_28),
    .out_3(collisione_muri_1_out_3));
  DotMatrix #(.matrixcols(1), .matrixrows(15)) dotmatrix_1 (.col0(fsm_1_out_4));
  DotMatrix #(.matrixcols(25), .matrixrows(15)) dotmatrix_2 (
    .col0(movimento_muri_1_out_28), .col1(movimento_muri_1_out_27), .col2(movimento_muri_1_out_26),
    .col3(movimento_muri_1_out_25), .col4(movimento_muri_1_out_24), .col5(movimento_muri_1_out_23),
    .col6(movimento_muri_1_out_22), .col7(movimento_muri_1_out_21), .col8(movimento_muri_1_out_20),
    .col9(movimento_muri_1_out_19), .col10(movimento_muri_1_out_18), .col11(movimento_muri_1_out_17),
    .col12(movimento_muri_1_out_16), .col13(movimento_muri_1_out_15), .col14(movimento_muri_1_out_14),
    .col15(movimento_muri_1_out_13), .col16(movimento_muri_1_out_12), .col17(movimento_muri_1_out_11),
    .col18(movimento_muri_1_out_10), .col19(movimento_muri_1_out_9), .col20(movimento_muri_1_out_8),
    .col21(movimento_muri_1_out_7), .col22(movimento_muri_1_out_6), .col23(movimento_muri_1_out_5),
    .col24(movimento_muri_1_out_4));
  FSM fsm_1 (.Clock(clock_1_out), .up(button_out), .down(button_2_out), .out_4(fsm_1_out_4));
  Clock clock_1 (.out(clock_1_out));
  Movimento_muri movimento_muri_1 (
    .out_4(movimento_muri_1_out_4), .out_5(movimento_muri_1_out_5), .out_6(movimento_muri_1_out_6),
    .out_7(movimento_muri_1_out_7), .out_8(movimento_muri_1_out_8), .out_9(movimento_muri_1_out_9),
    .out_10(movimento_muri_1_out_10), .out_11(movimento_muri_1_out_11), .out_12(movimento_muri_1_out_12),
    .out_13(movimento_muri_1_out_13), .out_14(movimento_muri_1_out_14), .out_15(movimento_muri_1_out_15),
    .out_16(movimento_muri_1_out_16), .out_17(movimento_muri_1_out_17), .out_18(movimento_muri_1_out_18),
    .out_19(movimento_muri_1_out_19), .out_20(movimento_muri_1_out_20), .out_21(movimento_muri_1_out_21),
    .out_22(movimento_muri_1_out_22), .out_23(movimento_muri_1_out_23), .out_24(movimento_muri_1_out_24),
    .out_25(movimento_muri_1_out_25), .out_26(movimento_muri_1_out_26), .out_27(movimento_muri_1_out_27),
    .out_28(movimento_muri_1_out_28), .Up(button_out), .Down(button_2_out), .Clock(and_1_out));
  and and_1 (and_1_out, collisione_muri_1_out_3, clock_1_out);
  Punteggio punteggio_1 (
    .Ultimo_muro(movimento_muri_1_out_28), .Collisione(collisione_muri_1_out_3), .out_3(punteggio_1_out_3));
  // Probe on punteggio_1_out_3
endmodule

module Generatore_muri (
  input  in_1,
  output [14:0] out_2
);

  wire comparator_1_gt;
  wire [3:0] multiplexer_1_out, random_1_out, subtractor_1_out;
  wire [14:0] muro_vero_1_out_2;

  Random #(.width(4)) random_1 (.clk(in_1), .out(random_1_out));  // open: next, clr
  Comparator #(.width(4), .mode("unsigned")) comparator_1 (
    .a(random_1_out), .b(4'b1010), .gt(comparator_1_gt));  // open: eq, lt
  Multiplexer #(.width(4)) multiplexer_1 (
    .in0(4'b0000), .in1(4'b0101), .out(multiplexer_1_out), .sel(comparator_1_gt));  // open: en
  Subtractor #(.width(4)) subtractor_1 (
    .a(random_1_out), .b(multiplexer_1_out), .out(subtractor_1_out));  // open: bin, bout
  Muro_vero muro_vero_1 (.in_1(subtractor_1_out), .out_2(muro_vero_1_out_2));
  assign out_2 = ~muro_vero_1_out_2;  // NOT_Gate not_1, 15 bits wide
endmodule

module Muro_vero (
  input  [3:0] in_1,
  output [14:0] out_2
);

  wire [3:0] adder_1_out, adder_2_out, adder_3_out, adder_4_out;
  wire [14:0] adder_5_out, adder_6_out, adder_7_out, decoder_1_out0, decoder_2_out0, decoder_3_out0,
       decoder_4_out0, decoder_5_out0;

  Adder #(.width(4)) adder_1 (.a(in_1), .b(4'b0001), .out(adder_1_out));  // open: cin, cout
  Adder #(.width(4)) adder_2 (.a(in_1), .b(4'b0010), .out(adder_2_out));  // open: cin, cout
  Adder #(.width(4)) adder_3 (.a(in_1), .b(4'b0011), .out(adder_3_out));  // open: cin, cout
  Adder #(.width(4)) adder_4 (.a(in_1), .b(4'b0100), .out(adder_4_out));  // open: cin, cout
  Decoder #(.select(4)) decoder_1 (
    .out0(decoder_1_out0[0]), .out1(decoder_1_out0[1]), .out2(decoder_1_out0[2]), .out3(decoder_1_out0[3]),
    .out4(decoder_1_out0[4]), .out5(decoder_1_out0[5]), .out6(decoder_1_out0[6]), .out7(decoder_1_out0[7]),
    .out8(decoder_1_out0[8]), .out9(decoder_1_out0[9]), .out10(decoder_1_out0[10]),
    .out11(decoder_1_out0[11]), .out12(decoder_1_out0[12]), .out13(decoder_1_out0[13]),
    .out14(decoder_1_out0[14]), .sel(in_1));  // open: out15, en
  Decoder #(.select(4)) decoder_2 (
    .out0(decoder_2_out0[0]), .out1(decoder_2_out0[1]), .out2(decoder_2_out0[2]), .out3(decoder_2_out0[3]),
    .out4(decoder_2_out0[4]), .out5(decoder_2_out0[5]), .out6(decoder_2_out0[6]), .out7(decoder_2_out0[7]),
    .out8(decoder_2_out0[8]), .out9(decoder_2_out0[9]), .out10(decoder_2_out0[10]),
    .out11(decoder_2_out0[11]), .out12(decoder_2_out0[12]), .out13(decoder_2_out0[13]),
    .out14(decoder_2_out0[14]), .sel(adder_1_out));  // open: out15, en
  Decoder #(.select(4)) decoder_3 (
    .out0(decoder_3_out0[0]), .out1(decoder_3_out0[1]), .out2(decoder_3_out0[2]), .out3(decoder_3_out0[3]),
    .out4(decoder_3_out0[4]), .out5(decoder_3_out0[5]), .out6(decoder_3_out0[6]), .out7(decoder_3_out0[7]),
    .out8(decoder_3_out0[8]), .out9(decoder_3_out0[9]), .out10(decoder_3_out0[10]),
    .out11(decoder_3_out0[11]), .out12(decoder_3_out0[12]), .out13(decoder_3_out0[13]),
    .out14(decoder_3_out0[14]), .sel(adder_2_out));  // open: out15, en
  Decoder #(.select(4)) decoder_4 (
    .out0(decoder_4_out0[0]), .out1(decoder_4_out0[1]), .out2(decoder_4_out0[2]), .out3(decoder_4_out0[3]),
    .out4(decoder_4_out0[4]), .out5(decoder_4_out0[5]), .out6(decoder_4_out0[6]), .out7(decoder_4_out0[7]),
    .out8(decoder_4_out0[8]), .out9(decoder_4_out0[9]), .out10(decoder_4_out0[10]),
    .out11(decoder_4_out0[11]), .out12(decoder_4_out0[12]), .out13(decoder_4_out0[13]),
    .out14(decoder_4_out0[14]), .sel(adder_3_out));  // open: out15, en
  Decoder #(.select(4)) decoder_5 (
    .out0(decoder_5_out0[0]), .out1(decoder_5_out0[1]), .out2(decoder_5_out0[2]), .out3(decoder_5_out0[3]),
    .out4(decoder_5_out0[4]), .out5(decoder_5_out0[5]), .out6(decoder_5_out0[6]), .out7(decoder_5_out0[7]),
    .out8(decoder_5_out0[8]), .out9(decoder_5_out0[9]), .out10(decoder_5_out0[10]),
    .out11(decoder_5_out0[11]), .out12(decoder_5_out0[12]), .out13(decoder_5_out0[13]),
    .out14(decoder_5_out0[14]), .sel(adder_4_out));  // open: out15, en
  Adder #(.width(15)) adder_5 (.a(decoder_1_out0), .b(decoder_2_out0), .out(adder_5_out));  // open: cin, cout
  Adder #(.width(15)) adder_6 (.a(adder_5_out), .b(decoder_3_out0), .out(adder_6_out));  // open: cin, cout
  Adder #(.width(15)) adder_7 (.a(adder_6_out), .b(decoder_4_out0), .out(adder_7_out));  // open: cin, cout
  Adder #(.width(15)) adder_8 (.a(adder_7_out), .b(decoder_5_out0), .out(out_2));  // open: cin, cout
endmodule

module Registro (
  input  in_1,
  input  [14:0] in_2,
  output [14:0] out_3
);

  D_Flip_Flop d_ff_1 (.clk(in_1), .D(in_2[0]), .Q(out_3[0]));  // open: Qn, preset, en, reset
  D_Flip_Flop d_ff_2 (.clk(in_1), .D(in_2[1]), .Q(out_3[1]));  // open: Qn, preset, en, reset
  D_Flip_Flop d_ff_3 (.clk(in_1), .D(in_2[2]), .Q(out_3[2]));  // open: Qn, preset, en, reset
  D_Flip_Flop d_ff_4 (.clk(in_1), .D(in_2[3]), .Q(out_3[3]));  // open: Qn, preset, en, reset
  D_Flip_Flop d_ff_5 (.clk(in_1), .D(in_2[4]), .Q(out_3[4]));  // open: Qn, preset, en, reset
  D_Flip_Flop d_ff_6 (.clk(in_1), .D(in_2[5]), .Q(out_3[5]));  // open: Qn, preset, en, reset
  D_Flip_Flop d_ff_7 (.clk(in_1), .D(in_2[6]), .Q(out_3[6]));  // open: Qn, preset, en, reset
  D_Flip_Flop d_ff_8 (.clk(in_1), .D(in_2[7]), .Q(out_3[7]));  // open: Qn, preset, en, reset
  D_Flip_Flop d_ff_9 (.clk(in_1), .D(in_2[8]), .Q(out_3[8]));  // open: Qn, preset, en, reset
  D_Flip_Flop d_ff_10 (.clk(in_1), .D(in_2[9]), .Q(out_3[9]));  // open: Qn, preset, en, reset
  D_Flip_Flop d_ff_11 (.clk(in_1), .D(in_2[10]), .Q(out_3[10]));  // open: Qn, preset, en, reset
  D_Flip_Flop d_ff_12 (.clk(in_1), .D(in_2[11]), .Q(out_3[11]));  // open: Qn, preset, en, reset
  D_Flip_Flop d_ff_13 (.clk(in_1), .D(in_2[12]), .Q(out_3[12]));  // open: Qn, preset, en, reset
  D_Flip_Flop d_ff_14 (.clk(in_1), .D(in_2[13]), .Q(out_3[13]));  // open: Qn, preset, en, reset
  D_Flip_Flop d_ff_15 (.clk(in_1), .D(in_2[14]), .Q(out_3[14]));  // open: Qn, preset, en, reset
endmodule

module Movimento_muri (
  input  Clock,
  input  Up,
  input  Down,
  output [14:0] out_4,
  output [14:0] out_5,
  output [14:0] out_6,
  output [14:0] out_7,
  output [14:0] out_8,
  output [14:0] out_9,
  output [14:0] out_10,
  output [14:0] out_11,
  output [14:0] out_12,
  output [14:0] out_13,
  output [14:0] out_14,
  output [14:0] out_15,
  output [14:0] out_16,
  output [14:0] out_17,
  output [14:0] out_18,
  output [14:0] out_19,
  output [14:0] out_20,
  output [14:0] out_21,
  output [14:0] out_22,
  output [14:0] out_23,
  output [14:0] out_24,
  output [14:0] out_25,
  output [14:0] out_26,
  output [14:0] out_27,
  output [14:0] out_28
);

  wire and_1_out, comparator_1_eq, counter_1_q, multiplexer_1_out, or_1_out;
  wire [2:0] counter_2_q;
  wire [14:0] generatore_muri_1_out_2, multiplexer_2_out;

  Generatore_muri generatore_muri_1 (.in_1(and_1_out), .out_2(generatore_muri_1_out_2));
  or or_1 (or_1_out, Up, Down);
  Counter #(.width(1), .max('h1), .ongoal("stay")) counter_1 (
    .Q(counter_1_q), .clk(or_1_out));  // open: load, D, count, carry, clr
  and and_1 (and_1_out, Clock, comparator_1_eq);
  Comparator #(.width(1)) comparator_1 (.a(counter_1_q), .b(1'b1), .eq(comparator_1_eq));  // open: gt, lt
  Counter #(.width(3), .max('h7)) counter_2 (.Q(counter_2_q), .clk(and_1_out));  // open: load, D, count, carry, clr
  Multiplexer #(.select(3)) multiplexer_1 (
    .in0(1'b1), .in1(1'b0), .in2(1'b0), .in3(1'b0), .in4(1'b0), .in5(1'b0), .in6(1'b0), .in7(1'b0),
    .out(multiplexer_1_out), .sel(counter_2_q));  // open: en
  Multiplexer #(.width(15)) multiplexer_2 (
    .in0({15{1'b0}}), .in1(generatore_muri_1_out_2), .out(multiplexer_2_out), .sel(multiplexer_1_out));  // open: en
  Registro registro_1 (.in_1(and_1_out), .in_2(multiplexer_2_out), .out_3(out_4));
  Registro registro_2 (.in_1(and_1_out), .in_2(out_4), .out_3(out_5));
  Registro registro_3 (.in_1(and_1_out), .in_2(out_5), .out_3(out_6));
  Registro registro_4 (.in_1(and_1_out), .in_2(out_6), .out_3(out_7));
  Registro registro_5 (.in_1(and_1_out), .in_2(out_7), .out_3(out_8));
  Registro registro_6 (.in_1(and_1_out), .in_2(out_8), .out_3(out_9));
  Registro registro_7 (.in_1(and_1_out), .in_2(out_9), .out_3(out_10));
  Registro registro_8 (.in_1(and_1_out), .in_2(out_10), .out_3(out_11));
  Registro registro_9 (.in_1(and_1_out), .in_2(out_11), .out_3(out_12));
  Registro registro_10 (.in_1(and_1_out), .in_2(out_12), .out_3(out_13));
  Registro registro_11 (.in_1(and_1_out), .in_2(out_13), .out_3(out_14));
  Registro registro_12 (.in_1(and_1_out), .in_2(out_14), .out_3(out_15));
  Registro registro_13 (.in_1(and_1_out), .in_2(out_15), .out_3(out_16));
  Registro registro_14 (.in_1(and_1_out), .in_2(out_16), .out_3(out_17));
  Registro registro_15 (.in_1(and_1_out), .in_2(out_17), .out_3(out_18));
  Registro registro_16 (.in_1(and_1_out), .in_2(out_18), .out_3(out_19));
  Registro registro_17 (.in_1(and_1_out), .in_2(out_19), .out_3(out_20));
  Registro registro_18 (.in_1(and_1_out), .in_2(out_20), .out_3(out_21));
  Registro registro_19 (.in_1(and_1_out), .in_2(out_21), .out_3(out_22));
  Registro registro_20 (.in_1(and_1_out), .in_2(out_22), .out_3(out_23));
  Registro registro_21 (.in_1(and_1_out), .in_2(out_23), .out_3(out_24));
  Registro registro_22 (.in_1(and_1_out), .in_2(out_24), .out_3(out_25));
  Registro registro_23 (.in_1(and_1_out), .in_2(out_25), .out_3(out_26));
  Registro registro_24 (.in_1(and_1_out), .in_2(out_26), .out_3(out_27));
  Registro registro_25 (.in_1(and_1_out), .in_2(out_27), .out_3(out_28));

  // Notes on the sheet:
  //   Generatore di muri
  //   Memoria
endmodule

module Movimento_personaggio (
  input  q3,
  input  q2,
  input  q1,
  input  q0,
  input  i1,
  input  i0,
  output q3_next,
  output q2_next,
  output q1_next,
  output q0_next
);

  wire and_1_out, and_2_out, and_3_out, and_4_out, and_5_out, and_6_out, and_7_out, and_8_out, and_9_out,
       and_10_out, and_11_out, and_12_out, and_13_out, and_14_out, and_15_out, and_16_out, and_17_out,
       and_18_out, and_19_out, and_20_out, and_21_out, and_22_out, and_23_out, and_24_out, and_25_out,
       and_26_out, and_27_out, and_28_out, and_29_out, not_1_out, not_2_out, not_3_out, not_4_out, not_5_out,
       not_6_out, not_7_out, not_8_out, not_9_out, not_10_out, not_11_out, not_12_out, not_13_out,
       not_14_out, not_15_out, not_16_out, not_17_out, not_18_out, not_19_out, not_20_out, not_21_out,
       not_22_out, not_23_out, not_24_out, not_25_out, not_26_out, not_27_out, not_28_out, not_29_out,
       not_30_out, not_31_out, not_32_out, not_33_out, not_34_out, not_35_out, not_36_out, not_37_out,
       not_38_out, not_39_out, not_40_out;

  not not_1 (not_1_out, q3);
  not not_2 (not_2_out, q2);
  not not_3 (not_3_out, q1);
  not not_4 (not_4_out, q0);
  not not_5 (not_5_out, q2);
  not not_6 (not_6_out, q1);
  not not_7 (not_7_out, q0);
  not not_8 (not_8_out, i0);
  not not_9 (not_9_out, q2);
  not not_10 (not_10_out, q1);
  not not_11 (not_11_out, i0);
  not not_12 (not_12_out, q0);
  not not_13 (not_13_out, i0);
  not not_14 (not_14_out, q1);
  not not_15 (not_15_out, i1);
  not not_16 (not_16_out, q2);
  not not_17 (not_17_out, q1);
  not not_18 (not_18_out, q0);
  not not_19 (not_19_out, i0);
  not not_20 (not_20_out, q1);
  not not_21 (not_21_out, q0);
  not not_22 (not_22_out, i0);
  not not_23 (not_23_out, i1);
  not not_24 (not_24_out, q1);
  not not_25 (not_25_out, q0);
  not not_26 (not_26_out, q1);
  not not_27 (not_27_out, q0);
  not not_28 (not_28_out, i0);
  not not_29 (not_29_out, q3);
  not not_30 (not_30_out, q2);
  not not_31 (not_31_out, q1);
  not not_32 (not_32_out, i1);
  not not_33 (not_33_out, i1);
  not not_34 (not_34_out, i0);
  not not_35 (not_35_out, q0);
  not not_36 (not_36_out, q0);
  not not_37 (not_37_out, q0);
  not not_38 (not_38_out, q0);
  not not_39 (not_39_out, q0);
  not not_40 (not_40_out, q0);
  and and_1 (and_1_out, not_1_out, not_2_out, not_3_out, not_4_out, i0);
  and and_2 (and_2_out, not_5_out, not_6_out, not_7_out, i1);
  and and_3 (and_3_out, q2, q1, q0, i1);
  and and_4 (and_4_out, q3, not_8_out);
  and and_5 (and_5_out, q3, q0);
  and and_6 (and_6_out, q3, q1);
  and and_7 (and_7_out, q3, q2);
  and and_8 (and_8_out, not_9_out, q1, q0, i1);
  and and_9 (and_9_out, q2, not_10_out, not_11_out);
  and and_10 (and_10_out, q2, not_12_out, not_13_out);
  and and_11 (and_11_out, q2, not_14_out, q0);
  and and_12 (and_12_out, q2, q1, not_15_out);
  and and_13 (and_13_out, q3, not_16_out, not_17_out, not_18_out, i0);
  and and_14 (and_14_out, q3, q2, not_19_out);
  and and_15 (and_15_out, not_20_out, q0, i1);
  and and_16 (and_16_out, q1, not_21_out, not_22_out);
  and and_17 (and_17_out, q1, q0, not_23_out);
  and and_18 (and_18_out, q2, not_24_out, not_25_out, i0);
  and and_19 (and_19_out, q3, not_26_out, not_27_out, i0);
  and and_20 (and_20_out, q3, q2, q1, not_28_out);
  and and_21 (and_21_out, not_29_out, not_30_out, not_31_out, q0, not_32_out);
  and and_22 (and_22_out, q0, not_33_out, not_34_out);
  and and_23 (and_23_out, q1, not_35_out, i0);
  and and_24 (and_24_out, q1, not_36_out, i1);
  and and_25 (and_25_out, q2, not_37_out, i0);
  and and_26 (and_26_out, q2, not_38_out, i1);
  and and_27 (and_27_out, q3, not_39_out, i0);
  and and_28 (and_28_out, q3, not_40_out, i1);
  and and_29 (and_29_out, q3, q2, q1, i1);
  or or_1 (q3_next, and_1_out, and_2_out, and_3_out, and_4_out, and_5_out, and_6_out, and_7_out);
  or or_2 (q2_next, and_8_out, and_9_out, and_10_out, and_11_out, and_12_out, and_13_out, and_14_out);
  or or_3 (q1_next, and_15_out, and_16_out, and_17_out, and_18_out, and_19_out, and_20_out);
  or or_4 (q0_next, and_21_out, and_22_out, and_23_out, and_24_out, and_25_out, and_26_out, and_27_out, and_28_out, and_29_out);
endmodule

module FSM (
  input  Clock,
  input  up,
  input  down,
  output [14:0] out_4
);

  wire d_ff_1_q, d_ff_2_q, d_ff_3_q, d_ff_4_q, movimento_personaggio_1_q0_next,
       movimento_personaggio_1_q1_next, movimento_personaggio_1_q2_next, movimento_personaggio_1_q3_next;

  Movimento_personaggio movimento_personaggio_1 (
    .q3(d_ff_1_q), .q2(d_ff_2_q), .q1(d_ff_3_q), .q0(d_ff_4_q), .i1(down), .i0(up),
    .q3_next(movimento_personaggio_1_q3_next), .q2_next(movimento_personaggio_1_q2_next),
    .q1_next(movimento_personaggio_1_q1_next), .q0_next(movimento_personaggio_1_q0_next));
  D_Flip_Flop d_ff_1 (.clk(Clock), .D(movimento_personaggio_1_q3_next), .Q(d_ff_1_q));  // open: Qn, preset, en, reset
  D_Flip_Flop d_ff_2 (.clk(Clock), .D(movimento_personaggio_1_q2_next), .Q(d_ff_2_q));  // open: Qn, preset, en, reset
  D_Flip_Flop d_ff_3 (.clk(Clock), .D(movimento_personaggio_1_q1_next), .Q(d_ff_3_q));  // open: Qn, preset, en, reset
  D_Flip_Flop d_ff_4 (.clk(Clock), .D(movimento_personaggio_1_q0_next), .Q(d_ff_4_q));  // open: Qn, preset, en, reset
  Funzione_di_uscita funzione_di_uscita_1 (.q3(d_ff_1_q), .q2(d_ff_2_q), .q1(d_ff_3_q), .q0(d_ff_4_q), .out_5(out_4));
endmodule

module Funzione_di_uscita (
  input  q3,
  input  q2,
  input  q1,
  input  q0,
  output [14:0] out_5
);

  and and_1 (out_5[14], ~q3, ~q2, ~q1, q0);  // AND_Gate
  and and_2 (out_5[13], ~q3, ~q2, q1, ~q0);  // AND_Gate
  and and_3 (out_5[12], ~q3, ~q2, q1, q0);  // AND_Gate
  and and_4 (out_5[11], ~q3, q2, ~q1, ~q0);  // AND_Gate
  and and_5 (out_5[10], ~q3, q2, ~q1, q0);  // AND_Gate
  and and_6 (out_5[9], ~q3, q2, q1, ~q0);  // AND_Gate
  and and_7 (out_5[8], ~q3, q2, q1, q0);  // AND_Gate
  and and_8 (out_5[7], q3, ~q2, ~q1, ~q0);  // AND_Gate
  and and_9 (out_5[6], q3, ~q2, ~q1, q0);  // AND_Gate
  and and_10 (out_5[5], q3, ~q2, q1, ~q0);  // AND_Gate
  and and_11 (out_5[4], q3, ~q2, q1, q0);  // AND_Gate
  and and_12 (out_5[3], q3, q2, ~q1, ~q0);  // AND_Gate
  and and_13 (out_5[2], q3, q2, ~q1, q0);  // AND_Gate
  and and_14 (out_5[1], q3, q2, q1, ~q0);  // AND_Gate
  and and_15 (out_5[0], q3, q2, q1, q0);
endmodule

module Collisione_muri (
  input  [14:0] Posizione_personaggio,
  input  [14:0] Posizione_muro,
  output out_3
);

  wire and_1_out, and_2_out, and_3_out, and_4_out, and_5_out, and_6_out, and_7_out, and_8_out, and_9_out,
       and_10_out, and_11_out, and_12_out, and_13_out, and_14_out, and_15_out, or_1_out;

  and and_1 (and_1_out, Posizione_personaggio[0], Posizione_muro[0]);
  and and_2 (and_2_out, Posizione_personaggio[1], Posizione_muro[1]);
  and and_3 (and_3_out, Posizione_personaggio[2], Posizione_muro[2]);
  and and_4 (and_4_out, Posizione_personaggio[3], Posizione_muro[3]);
  and and_5 (and_5_out, Posizione_personaggio[4], Posizione_muro[4]);
  and and_6 (and_6_out, Posizione_personaggio[5], Posizione_muro[5]);
  and and_7 (and_7_out, Posizione_personaggio[6], Posizione_muro[6]);
  and and_8 (and_8_out, Posizione_personaggio[7], Posizione_muro[7]);
  and and_9 (and_9_out, Posizione_personaggio[8], Posizione_muro[8]);
  and and_10 (and_10_out, Posizione_personaggio[9], Posizione_muro[9]);
  and and_11 (and_11_out, Posizione_personaggio[10], Posizione_muro[10]);
  and and_12 (and_12_out, Posizione_personaggio[11], Posizione_muro[11]);
  and and_13 (and_13_out, Posizione_personaggio[12], Posizione_muro[12]);
  and and_14 (and_14_out, Posizione_personaggio[13], Posizione_muro[13]);
  and and_15 (and_15_out, Posizione_personaggio[14], Posizione_muro[14]);
  or or_1 (or_1_out, and_1_out, and_2_out, and_3_out, and_4_out, and_5_out, and_6_out, and_7_out, and_8_out, and_9_out, and_10_out, and_11_out, and_12_out, and_13_out, and_14_out, and_15_out);
  not not_1 (out_3, or_1_out);
endmodule

module Punteggio (
  input  [14:0] Ultimo_muro,
  input  Collisione,
  output [7:0] out_3
);

  wire and_1_out, comparator_1_gt;

  Comparator #(.width(15), .mode("unsigned")) comparator_1 (
    .a(Ultimo_muro), .b({15{1'b0}}), .gt(comparator_1_gt));  // open: eq, lt
  and and_1 (and_1_out, comparator_1_gt, Collisione);
  Counter counter_1 (.Q(out_3), .clk(and_1_out));  // open: load, D, count, carry, clr
endmodule
